// Logisim project SignedMultipier.circ as structural Verilog: 4 circuits, main circuit main
module main (
  input  [7:0] a,
  input  [7:0] b,
  output [15:0] out_3
);

  wire eightbitstc_1_c, eightbitstc_1_c1, eightbitstc_1_c2, eightbitstc_1_c3, eightbitstc_1_c4,
       eightbitstc_1_c5, eightbitstc_1_c6, eightbitstc_1_c7, eightbitstc_2_c, eightbitstc_2_c1,
       eightbitstc_2_c2, eightbitstc_2_c3, eightbitstc_2_c4, eightbitstc_2_c5, eightbitstc_2_c6,
       eightbitstc_2_c7, unsignedmultilplier_1_p, unsignedmultilplier_1_p1, unsignedmultilplier_1_p2,
       unsignedmultilplier_1_p3, unsignedmultilplier_1_p4, unsignedmultilplier_1_p5,
       unsignedmultilplier_1_p6, unsignedmultilplier_1_p7, unsignedmultilplier_1_p8,
       unsignedmultilplier_1_p9, unsignedmultilplier_1_p10, unsignedmultilplier_1_p11,
       unsignedmultilplier_1_p12, unsignedmultilplier_1_p13, unsignedmultilplier_1_p14,
       unsignedmultilplier_1_p15;

  eightBitsTC eightbitstc_1 (
    .a7(a[7]), .a6(a[6]), .a5(a[5]), .a4(a[4]), .a3(a[3]), .a2(a[2]), .a1(a[1]), .a(a[0]),
    .c7(eightbitstc_1_c7), .c6(eightbitstc_1_c6), .c5(eightbitstc_1_c5), .c4(eightbitstc_1_c4),
    .c3(eightbitstc_1_c3), .c2(eightbitstc_1_c2), .c1(eightbitstc_1_c1), .c(eightbitstc_1_c));
  eightBitsTC eightbitstc_2 (
    .a7(b[7]), .a6(b[6]), .a5(b[5]), .a4(b[4]), .a3(b[3]), .a2(b[2]), .a1(b[1]), .a(b[0]),
    .c7(eightbitstc_2_c7), .c6(eightbitstc_2_c6), .c5(eightbitstc_2_c5), .c4(eightbitstc_2_c4),
    .c3(eightbitstc_2_c3), .c2(eightbitstc_2_c2), .c1(eightbitstc_2_c1), .c(eightbitstc_2_c));
  UnsignedMultilplier unsignedmultilplier_1 (
    .b7(eightbitstc_1_c7), .b6(eightbitstc_1_c6), .b5(eightbitstc_1_c5), .b4(eightbitstc_1_c4),
    .b3(eightbitstc_1_c3), .b2(eightbitstc_1_c2), .b1(eightbitstc_1_c1), .b0(eightbitstc_1_c),
    .a7(eightbitstc_2_c7), .a6(eightbitstc_2_c6), .a5(eightbitstc_2_c5), .a4(eightbitstc_2_c4),
    .a3(eightbitstc_2_c3), .a2(eightbitstc_2_c2), .a1(eightbitstc_2_c1), .a0(eightbitstc_2_c),
    .p15(unsignedmultilplier_1_p15), .p14(unsignedmultilplier_1_p14), .p13(unsignedmultilplier_1_p13),
    .p12(unsignedmultilplier_1_p12), .p11(unsignedmultilplier_1_p11), .p10(unsignedmultilplier_1_p10),
    .p9(unsignedmultilplier_1_p9), .p8(unsignedmultilplier_1_p8), .p7(unsignedmultilplier_1_p7),
    .p6(unsignedmultilplier_1_p6), .p5(unsignedmultilplier_1_p5), .p4(unsignedmultilplier_1_p4),
    .p3(unsignedmultilplier_1_p3), .p2(unsignedmultilplier_1_p2), .p1(unsignedmultilplier_1_p1),
    .p(unsignedmultilplier_1_p));
  TC_16 tc_16_1 (
    .a15(unsignedmultilplier_1_p15), .a14(unsignedmultilplier_1_p14), .a13(unsignedmultilplier_1_p13),
    .a12(unsignedmultilplier_1_p12), .a11(unsignedmultilplier_1_p11), .a10(unsignedmultilplier_1_p10),
    .a9(unsignedmultilplier_1_p9), .a8(unsignedmultilplier_1_p8), .a7(unsignedmultilplier_1_p7),
    .a6(unsignedmultilplier_1_p6), .a5(unsignedmultilplier_1_p5), .a4(unsignedmultilplier_1_p4),
    .a3(unsignedmultilplier_1_p3), .a2(unsignedmultilplier_1_p2), .a1(unsignedmultilplier_1_p1),
    .a0(unsignedmultilplier_1_p), .MS_2(b[7]), .MS_1(a[7]), .c15(out_3[15]), .c14(out_3[14]),
    .c13(out_3[13]), .c12(out_3[12]), .c11(out_3[11]), .c10(out_3[10]), .c9(out_3[9]), .c8(out_3[8]),
    .c7(out_3[7]), .c6(out_3[6]), .c5(out_3[5]), .c4(out_3[4]), .c3(out_3[3]), .c2(out_3[2]), .c1(out_3[1]),
    .c0(out_3[0]));
endmodule

module eightBitsTC (
  input  a7,
  input  a6,
  input  a5,
  input  a4,
  input  a3,
  input  a2,
  input  a1,
  input  a,
  output c7,
  output c6,
  output c5,
  output c4,
  output c3,
  output c2,
  output c1,
  output c
);

  wire adder_1_cout, adder_1_out, adder_2_cout, adder_2_out, adder_3_cout, adder_3_out, adder_4_cout,
       adder_4_out, adder_5_cout, adder_5_out, adder_6_cout, adder_6_out, adder_7_cout, adder_7_out,
       adder_8_cout, adder_8_out, not_1_out, not_2_out, not_3_out, not_4_out, not_5_out, not_6_out,
       not_7_out, not_8_out;

  not not_1 (not_1_out, a7);
  Adder #(.width(1)) adder_1 (.a(not_1_out), .b(1'b0), .out(adder_1_out), .cin(adder_2_cout), .cout(adder_1_cout));
  Multiplexer multiplexer_1 (.in0(a7), .in1(adder_1_out), .out(c7), .sel(a7));
  not not_2 (not_2_out, a6);
  Adder #(.width(1)) adder_2 (.a(not_2_out), .b(1'b0), .out(adder_2_out), .cin(adder_3_cout), .cout(adder_2_cout));
  Multiplexer multiplexer_2 (.in0(a6), .in1(adder_2_out), .out(c6), .sel(a7));
  not not_3 (not_3_out, a5);
  Adder #(.width(1)) adder_3 (.a(not_3_out), .b(1'b0), .out(adder_3_out), .cin(adder_4_cout), .cout(adder_3_cout));
  Multiplexer multiplexer_3 (.in0(a5), .in1(adder_3_out), .out(c5), .sel(a7));
  not not_4 (not_4_out, a4);
  Adder #(.width(1)) adder_4 (.a(not_4_out), .b(1'b0), .out(adder_4_out), .cin(adder_5_cout), .cout(adder_4_cout));
  Multiplexer multiplexer_4 (.in0(a4), .in1(adder_4_out), .out(c4), .sel(a7));
  not not_5 (not_5_out, a3);
  Adder #(.width(1)) adder_5 (.a(not_5_out), .b(1'b0), .out(adder_5_out), .cin(adder_6_cout), .cout(adder_5_cout));
  Multiplexer multiplexer_5 (.in0(a3), .in1(adder_5_out), .out(c3), .sel(a7));
  not not_6 (not_6_out, a2);
  Adder #(.width(1)) adder_6 (.a(not_6_out), .b(1'b0), .out(adder_6_out), .cin(adder_7_cout), .cout(adder_6_cout));
  Multiplexer multiplexer_6 (.in0(a2), .in1(adder_6_out), .out(c2), .sel(a7));
  not not_7 (not_7_out, a1);
  Adder #(.width(1)) adder_7 (.a(not_7_out), .b(1'b0), .out(adder_7_out), .cin(adder_8_cout), .cout(adder_7_cout));
  Multiplexer multiplexer_7 (.in0(a1), .in1(adder_7_out), .out(c1), .sel(a7));
  not not_8 (not_8_out, a);
  Adder #(.width(1)) adder_8 (.a(not_8_out), .b(1'b0), .out(adder_8_out), .cin(1'b1), .cout(adder_8_cout));
  Multiplexer multiplexer_8 (.in0(a), .in1(adder_8_out), .out(c), .sel(a7));
endmodule

module UnsignedMultilplier (
  input  b7,
  input  b6,
  input  b5,
  input  b4,
  input  b3,
  input  b2,
  input  b1,
  input  b0,
  input  a7,
  input  a6,
  input  a5,
  input  a4,
  input  a3,
  input  a2,
  input  a1,
  input  a0,
  output p15,
  output p14,
  output p13,
  output p12,
  output p11,
  output p10,
  output p9,
  output p8,
  output p7,
  output p6,
  output p5,
  output p4,
  output p3,
  output p2,
  output p1,
  output p
);

  wire adder_2_cout, adder_2_out, adder_3_cout, adder_4_cout, adder_4_out, adder_5_cout, adder_5_out,
       adder_6_cout, adder_7_cout, adder_7_out, adder_8_cout, adder_8_out, adder_9_cout, adder_9_out,
       adder_10_cout, adder_11_cout, adder_11_out, adder_12_cout, adder_12_out, adder_13_cout, adder_13_out,
       adder_14_cout, adder_14_out, adder_15_cout, adder_16_cout, adder_16_out, adder_17_cout, adder_17_out,
       adder_18_cout, adder_18_out, adder_19_cout, adder_19_out, adder_20_cout, adder_20_out, adder_21_cout,
       adder_22_cout, adder_22_out, adder_23_cout, adder_23_out, adder_24_cout, adder_24_out, adder_25_cout,
       adder_25_out, adder_26_cout, adder_26_out, adder_27_cout, adder_27_out, adder_28_cout, adder_29_cout,
       adder_29_out, adder_30_cout, adder_30_out, adder_31_cout, adder_31_out, adder_32_cout, adder_32_out,
       adder_33_cout, adder_33_out, adder_34_cout, adder_34_out, adder_35_cout, adder_36_cout, adder_36_out,
       adder_37_cout, adder_37_out, adder_38_cout, adder_38_out, adder_39_cout, adder_39_out, adder_40_cout,
       adder_40_out, adder_41_cout, adder_42_cout, adder_42_out, adder_43_cout, adder_43_out, adder_44_cout,
       adder_44_out, adder_45_cout, adder_45_out, adder_46_cout, adder_47_cout, adder_47_out, adder_48_cout,
       adder_48_out, adder_49_cout, adder_49_out, adder_50_cout, adder_51_cout, adder_51_out, adder_52_cout,
       adder_52_out, adder_53_cout, adder_54_cout, adder_54_out, adder_55_cout, adder_56_cout, and_1_out,
       and_2_out, and_3_out, and_4_out, and_5_out, and_6_out, and_7_out, and_8_out, and_9_out, and_10_out,
       and_11_out, and_12_out, and_13_out, and_14_out, and_15_out, and_16_out, and_17_out, and_18_out,
       and_19_out, and_20_out, and_21_out, and_22_out, and_23_out, and_24_out, and_25_out, and_26_out,
       and_27_out, and_28_out, and_29_out, and_30_out, and_31_out, and_32_out, and_33_out, and_34_out,
       and_35_out, and_36_out, and_37_out, and_38_out, and_39_out, and_40_out, and_41_out, and_42_out,
       and_43_out, and_44_out, and_45_out, and_46_out, and_47_out, and_48_out, and_49_out, and_50_out,
       and_51_out, and_52_out, and_53_out, and_54_out, and_55_out, and_56_out, and_57_out, and_58_out,
       and_59_out, and_60_out, and_61_out, and_62_out, and_63_out;

  and and_1 (and_1_out, a7, b7);
  Adder #(.width(1)) adder_1 (.a(adder_2_cout), .b(and_1_out), .out(p14), .cin(adder_3_cout), .cout(p15));
  and and_2 (and_2_out, a7, b6);
  and and_3 (and_3_out, a6, b7);
  Adder #(.width(1)) adder_2 (
    .a(adder_4_cout), .b(and_2_out), .out(adder_2_out), .cin(adder_5_cout), .cout(adder_2_cout));
  Adder #(.width(1)) adder_3 (.a(adder_2_out), .b(and_3_out), .out(p13), .cin(adder_6_cout), .cout(adder_3_cout));
  and and_4 (and_4_out, a7, b5);
  and and_5 (and_5_out, a6, b6);
  and and_6 (and_6_out, a5, b7);
  Adder #(.width(1)) adder_4 (
    .a(adder_7_cout), .b(and_4_out), .out(adder_4_out), .cin(adder_8_cout), .cout(adder_4_cout));
  Adder #(.width(1)) adder_5 (
    .a(adder_4_out), .b(and_5_out), .out(adder_5_out), .cin(adder_9_cout), .cout(adder_5_cout));
  Adder #(.width(1)) adder_6 (.a(adder_5_out), .b(and_6_out), .out(p12), .cin(adder_10_cout), .cout(adder_6_cout));
  and and_7 (and_7_out, a7, b4);
  and and_8 (and_8_out, a6, b5);
  and and_9 (and_9_out, a5, b6);
  and and_10 (and_10_out, a4, b7);
  Adder #(.width(1)) adder_7 (
    .a(adder_11_cout), .b(and_7_out), .out(adder_7_out), .cin(adder_12_cout), .cout(adder_7_cout));
  Adder #(.width(1)) adder_8 (
    .a(adder_7_out), .b(and_8_out), .out(adder_8_out), .cin(adder_13_cout), .cout(adder_8_cout));
  Adder #(.width(1)) adder_9 (
    .a(adder_8_out), .b(and_9_out), .out(adder_9_out), .cin(adder_14_cout), .cout(adder_9_cout));
  Adder #(.width(1)) adder_10 (.a(adder_9_out), .b(and_10_out), .out(p11), .cin(adder_15_cout), .cout(adder_10_cout));
  and and_11 (and_11_out, a7, b3);
  and and_12 (and_12_out, a6, b4);
  and and_13 (and_13_out, a5, b5);
  and and_14 (and_14_out, a4, b6);
  and and_15 (and_15_out, a3, b7);
  Adder #(.width(1)) adder_11 (
    .a(adder_18_cout), .b(and_11_out), .out(adder_11_out), .cin(adder_19_cout), .cout(adder_11_cout));
  Adder #(.width(1)) adder_12 (
    .a(adder_11_out), .b(and_12_out), .out(adder_12_out), .cin(adder_16_cout), .cout(adder_12_cout));
  Adder #(.width(1)) adder_13 (
    .a(adder_12_out), .b(and_13_out), .out(adder_13_out), .cin(adder_17_cout), .cout(adder_13_cout));
  Adder #(.width(1)) adder_14 (
    .a(adder_13_out), .b(and_14_out), .out(adder_14_out), .cin(adder_20_cout), .cout(adder_14_cout));
  Adder #(.width(1)) adder_15 (.a(adder_14_out), .b(and_15_out), .out(p10), .cin(adder_21_cout), .cout(adder_15_cout));
  and and_16 (and_16_out, a5, b4);
  and and_17 (and_17_out, a4, b5);
  and and_18 (and_18_out, a7, b2);
  and and_19 (and_19_out, a6, b3);
  Adder #(.width(1)) adder_16 (
    .a(adder_19_out), .b(and_16_out), .out(adder_16_out), .cin(adder_25_cout), .cout(adder_16_cout));
  Adder #(.width(1)) adder_17 (
    .a(adder_16_out), .b(and_17_out), .out(adder_17_out), .cin(adder_26_cout), .cout(adder_17_cout));
  and and_20 (and_20_out, a3, b6);
  and and_21 (and_21_out, a2, b7);
  Adder #(.width(1)) adder_18 (
    .a(adder_22_cout), .b(and_18_out), .out(adder_18_out), .cin(adder_23_cout), .cout(adder_18_cout));
  Adder #(.width(1)) adder_19 (
    .a(adder_18_out), .b(and_19_out), .out(adder_19_out), .cin(adder_24_cout), .cout(adder_19_cout));
  Adder #(.width(1)) adder_20 (
    .a(adder_17_out), .b(and_20_out), .out(adder_20_out), .cin(adder_27_cout), .cout(adder_20_cout));
  Adder #(.width(1)) adder_21 (.a(adder_20_out), .b(and_21_out), .out(p9), .cin(adder_28_cout), .cout(adder_21_cout));
  and and_22 (and_22_out, a7, b1);
  and and_23 (and_23_out, a6, b2);
  and and_24 (and_24_out, a5, b3);
  and and_25 (and_25_out, a4, b4);
  and and_26 (and_26_out, a3, b5);
  and and_27 (and_27_out, a2, b6);
  and and_28 (and_28_out, a1, b7);
  Adder #(.width(1)) adder_22 (.a(1'b0), .b(and_22_out), .out(adder_22_out), .cin(adder_29_cout), .cout(adder_22_cout));
  Adder #(.width(1)) adder_23 (
    .a(adder_22_out), .b(and_23_out), .out(adder_23_out), .cin(adder_30_cout), .cout(adder_23_cout));
  Adder #(.width(1)) adder_24 (
    .a(adder_23_out), .b(and_24_out), .out(adder_24_out), .cin(adder_31_cout), .cout(adder_24_cout));
  Adder #(.width(1)) adder_25 (
    .a(adder_24_out), .b(and_25_out), .out(adder_25_out), .cin(adder_32_cout), .cout(adder_25_cout));
  Adder #(.width(1)) adder_26 (
    .a(adder_25_out), .b(and_26_out), .out(adder_26_out), .cin(adder_33_cout), .cout(adder_26_cout));
  Adder #(.width(1)) adder_27 (
    .a(adder_26_out), .b(and_27_out), .out(adder_27_out), .cin(adder_34_cout), .cout(adder_27_cout));
  Adder #(.width(1)) adder_28 (.a(adder_27_out), .b(and_28_out), .out(p8), .cin(adder_35_cout), .cout(adder_28_cout));
  and and_29 (and_29_out, a6, b1);
  and and_30 (and_30_out, a7, b0);
  and and_31 (and_31_out, a5, b2);
  and and_32 (and_32_out, a4, b3);
  and and_33 (and_33_out, a3, b4);
  and and_34 (and_34_out, a2, b5);
  and and_35 (and_35_out, a1, b6);
  and and_36 (and_36_out, a0, b7);
  and and_37 (and_37_out, a5, b1);
  Adder #(.width(1)) adder_29 (
    .a(and_30_out), .b(and_29_out), .out(adder_29_out), .cin(adder_36_cout), .cout(adder_29_cout));
  Adder #(.width(1)) adder_30 (
    .a(adder_29_out), .b(and_31_out), .out(adder_30_out), .cin(adder_37_cout), .cout(adder_30_cout));
  Adder #(.width(1)) adder_31 (
    .a(adder_30_out), .b(and_32_out), .out(adder_31_out), .cin(adder_38_cout), .cout(adder_31_cout));
  Adder #(.width(1)) adder_32 (
    .a(adder_31_out), .b(and_33_out), .out(adder_32_out), .cin(adder_39_cout), .cout(adder_32_cout));
  Adder #(.width(1)) adder_33 (
    .a(adder_32_out), .b(and_34_out), .out(adder_33_out), .cin(adder_40_cout), .cout(adder_33_cout));
  Adder #(.width(1)) adder_34 (
    .a(adder_33_out), .b(and_35_out), .out(adder_34_out), .cin(adder_41_cout), .cout(adder_34_cout));
  Adder #(.width(1)) adder_35 (.a(adder_34_out), .b(and_36_out), .out(p7), .cin(1'b0), .cout(adder_35_cout));
  and and_38 (and_38_out, a6, b0);
  and and_39 (and_39_out, a4, b2);
  and and_40 (and_40_out, a3, b3);
  and and_41 (and_41_out, a2, b4);
  and and_42 (and_42_out, a1, b5);
  and and_43 (and_43_out, a0, b6);
  Adder #(.width(1)) adder_36 (
    .a(and_38_out), .b(and_37_out), .out(adder_36_out), .cin(adder_42_cout), .cout(adder_36_cout));
  Adder #(.width(1)) adder_37 (
    .a(adder_36_out), .b(and_39_out), .out(adder_37_out), .cin(adder_43_cout), .cout(adder_37_cout));
  Adder #(.width(1)) adder_38 (
    .a(adder_37_out), .b(and_40_out), .out(adder_38_out), .cin(adder_44_cout), .cout(adder_38_cout));
  Adder #(.width(1)) adder_39 (
    .a(adder_38_out), .b(and_41_out), .out(adder_39_out), .cin(adder_45_cout), .cout(adder_39_cout));
  Adder #(.width(1)) adder_40 (
    .a(adder_39_out), .b(and_42_out), .out(adder_40_out), .cin(adder_46_cout), .cout(adder_40_cout));
  Adder #(.width(1)) adder_41 (.a(adder_40_out), .b(and_43_out), .out(p6), .cin(1'b0), .cout(adder_41_cout));
  and and_44 (and_44_out, a4, b1);
  and and_45 (and_45_out, a5, b0);
  and and_46 (and_46_out, a3, b2);
  and and_47 (and_47_out, a2, b3);
  and and_48 (and_48_out, a1, b4);
  and and_49 (and_49_out, a0, b5);
  and and_50 (and_50_out, a3, b1);
  Adder #(.width(1)) adder_42 (
    .a(and_45_out), .b(and_44_out), .out(adder_42_out), .cin(adder_47_cout), .cout(adder_42_cout));
  Adder #(.width(1)) adder_43 (
    .a(adder_42_out), .b(and_46_out), .out(adder_43_out), .cin(adder_48_cout), .cout(adder_43_cout));
  Adder #(.width(1)) adder_44 (
    .a(adder_43_out), .b(and_47_out), .out(adder_44_out), .cin(adder_49_cout), .cout(adder_44_cout));
  Adder #(.width(1)) adder_45 (
    .a(adder_44_out), .b(and_48_out), .out(adder_45_out), .cin(adder_50_cout), .cout(adder_45_cout));
  Adder #(.width(1)) adder_46 (.a(adder_45_out), .b(and_49_out), .out(p5), .cin(1'b0), .cout(adder_46_cout));
  and and_51 (and_51_out, a4, b0);
  and and_52 (and_52_out, a2, b2);
  and and_53 (and_53_out, a1, b3);
  and and_54 (and_54_out, a0, b4);
  Adder #(.width(1)) adder_47 (
    .a(and_51_out), .b(and_50_out), .out(adder_47_out), .cin(adder_51_cout), .cout(adder_47_cout));
  Adder #(.width(1)) adder_48 (
    .a(adder_47_out), .b(and_52_out), .out(adder_48_out), .cin(adder_52_cout), .cout(adder_48_cout));
  Adder #(.width(1)) adder_49 (
    .a(adder_48_out), .b(and_53_out), .out(adder_49_out), .cin(adder_53_cout), .cout(adder_49_cout));
  Adder #(.width(1)) adder_50 (.a(adder_49_out), .b(and_54_out), .out(p4), .cin(1'b0), .cout(adder_50_cout));
  and and_55 (and_55_out, a2, b1);
  and and_56 (and_56_out, a3, b0);
  and and_57 (and_57_out, a1, b2);
  and and_58 (and_58_out, a0, b3);
  and and_59 (and_59_out, a1, b1);
  Adder #(.width(1)) adder_51 (
    .a(and_56_out), .b(and_55_out), .out(adder_51_out), .cin(adder_54_cout), .cout(adder_51_cout));
  Adder #(.width(1)) adder_52 (
    .a(adder_51_out), .b(and_57_out), .out(adder_52_out), .cin(adder_55_cout), .cout(adder_52_cout));
  Adder #(.width(1)) adder_53 (.a(adder_52_out), .b(and_58_out), .out(p3), .cin(1'b0), .cout(adder_53_cout));
  and and_60 (and_60_out, a2, b0);
  and and_61 (and_61_out, a0, b2);
  Adder #(.width(1)) adder_54 (
    .a(and_60_out), .b(and_59_out), .out(adder_54_out), .cin(adder_56_cout), .cout(adder_54_cout));
  Adder #(.width(1)) adder_55 (.a(adder_54_out), .b(and_61_out), .out(p2), .cin(1'b0), .cout(adder_55_cout));
  and and_62 (and_62_out, a0, b1);
  and and_63 (and_63_out, a1, b0);
  Adder #(.width(1)) adder_56 (.a(and_63_out), .b(and_62_out), .out(p1), .cin(1'b0), .cout(adder_56_cout));
  and and_64 (p, a0, b0);

  // Notes on the sheet:
  //   a7
  //   b1
  //   a6
  //   b1
  //   a5
  //   a4
  //   a3
  //   a2
  //   a1
  //   a0
  //   b0
  //   b2
  //   b3
  //   b4
  //   b5
  //   b6
  //   b7
  //   a5
  //   b1
  //   a4
  //   b2
  //   a3
  //   a2
  //   b4
  //   a1
  //   b5
  //   a0
  //   b6
  //   b0
  //   b3
  //   a4
  //   b1
  //   a3
  //   a2
  //   a1
  //   a0
  //   b0
  //   b2
  //   b3
  //   b4
  //   b5
  //   a3
  //   b1
  //   a2
  //   a1
  //   b3
  //   a0
  //   b4
  //   b0
  //   b2
  //   a2
  //   b1
  //   a1
  //   b0
  //   b2
  //   a0
  //   b3
  //   a1
  //   b1
  //   a0
  //   b0
  //   b2
  //   a0
  //   b1
  //   b0
  //   b0
endmodule

module TC_16 (
  input  a15,
  input  a14,
  input  a13,
  input  a12,
  input  a11,
  input  a10,
  input  a9,
  input  a8,
  input  a7,
  input  a6,
  input  a5,
  input  a4,
  input  a3,
  input  a2,
  input  a1,
  input  a0,
  input  MS_2,
  input  MS_1,
  output c15,
  output c14,
  output c13,
  output c12,
  output c11,
  output c10,
  output c9,
  output c8,
  output c7,
  output c6,
  output c5,
  output c4,
  output c3,
  output c2,
  output c1,
  output c0
);

  wire adder_1_cout, adder_1_out, adder_2_cout, adder_2_out, adder_3_cout, adder_3_out, adder_4_cout,
       adder_4_out, adder_5_cout, adder_5_out, adder_6_cout, adder_6_out, adder_7_cout, adder_7_out,
       adder_8_cout, adder_8_out, adder_9_cout, adder_9_out, adder_10_cout, adder_10_out, adder_11_cout,
       adder_11_out, adder_12_cout, adder_12_out, adder_13_cout, adder_13_out, adder_14_cout, adder_14_out,
       adder_15_cout, adder_15_out, adder_16_cout, adder_16_out, not_1_out, not_2_out, not_3_out, not_4_out,
       not_5_out, not_6_out, not_7_out, not_8_out, not_9_out, not_10_out, not_11_out, not_12_out, not_13_out,
       not_14_out, not_15_out, not_16_out, xor_1_out;

  xor xor_1 (xor_1_out, MS_2, MS_1);
  not not_1 (not_1_out, a15);
  Adder #(.width(1)) adder_1 (.a(not_1_out), .b(1'b0), .out(adder_1_out), .cin(adder_2_cout), .cout(adder_1_cout));
  Multiplexer multiplexer_1 (.in0(a15), .in1(adder_1_out), .out(c15), .sel(xor_1_out));
  not not_2 (not_2_out, a14);
  Adder #(.width(1)) adder_2 (.a(not_2_out), .b(1'b0), .out(adder_2_out), .cin(adder_3_cout), .cout(adder_2_cout));
  Multiplexer multiplexer_2 (.in0(a14), .in1(adder_2_out), .out(c14), .sel(xor_1_out));
  not not_3 (not_3_out, a13);
  Adder #(.width(1)) adder_3 (.a(not_3_out), .b(1'b0), .out(adder_3_out), .cin(adder_4_cout), .cout(adder_3_cout));
  Multiplexer multiplexer_3 (.in0(a13), .in1(adder_3_out), .out(c13), .sel(xor_1_out));
  not not_4 (not_4_out, a12);
  Adder #(.width(1)) adder_4 (.a(not_4_out), .b(1'b0), .out(adder_4_out), .cin(adder_5_cout), .cout(adder_4_cout));
  Multiplexer multiplexer_4 (.in0(a12), .in1(adder_4_out), .out(c12), .sel(xor_1_out));
  not not_5 (not_5_out, a11);
  Adder #(.width(1)) adder_5 (.a(not_5_out), .b(1'b0), .out(adder_5_out), .cin(adder_6_cout), .cout(adder_5_cout));
  Multiplexer multiplexer_5 (.in0(a11), .in1(adder_5_out), .out(c11), .sel(xor_1_out));
  not not_6 (not_6_out, a10);
  Adder #(.width(1)) adder_6 (.a(not_6_out), .b(1'b0), .out(adder_6_out), .cin(adder_7_cout), .cout(adder_6_cout));
  Multiplexer multiplexer_6 (.in0(a10), .in1(adder_6_out), .out(c10), .sel(xor_1_out));
  not not_7 (not_7_out, a9);
  Adder #(.width(1)) adder_7 (.a(not_7_out), .b(1'b0), .out(adder_7_out), .cin(adder_8_cout), .cout(adder_7_cout));
  Multiplexer multiplexer_7 (.in0(a9), .in1(adder_7_out), .out(c9), .sel(xor_1_out));
  not not_8 (not_8_out, a8);
  Adder #(.width(1)) adder_8 (.a(not_8_out), .b(1'b0), .out(adder_8_out), .cin(adder_9_cout), .cout(adder_8_cout));
  Multiplexer multiplexer_8 (.in0(a8), .in1(adder_8_out), .out(c8), .sel(xor_1_out));
  not not_9 (not_9_out, a7);
  Adder #(.width(1)) adder_9 (.a(not_9_out), .b(1'b0), .out(adder_9_out), .cin(adder_10_cout), .cout(adder_9_cout));
  Multiplexer multiplexer_9 (.in0(a7), .in1(adder_9_out), .out(c7), .sel(xor_1_out));
  not not_10 (not_10_out, a6);
  Adder #(.width(1)) adder_10 (.a(not_10_out), .b(1'b0), .out(adder_10_out), .cin(adder_11_cout), .cout(adder_10_cout));
  Multiplexer multiplexer_10 (.in0(a6), .in1(adder_10_out), .out(c6), .sel(xor_1_out));
  not not_11 (not_11_out, a5);
  Adder #(.width(1)) adder_11 (.a(not_11_out), .b(1'b0), .out(adder_11_out), .cin(adder_12_cout), .cout(adder_11_cout));
  Multiplexer multiplexer_11 (.in0(a5), .in1(adder_11_out), .out(c5), .sel(xor_1_out));
  not not_12 (not_12_out, a4);
  Adder #(.width(1)) adder_12 (.a(not_12_out), .b(1'b0), .out(adder_12_out), .cin(adder_13_cout), .cout(adder_12_cout));
  Multiplexer multiplexer_12 (.in0(a4), .in1(adder_12_out), .out(c4), .sel(xor_1_out));
  not not_13 (not_13_out, a3);
  Adder #(.width(1)) adder_13 (.a(not_13_out), .b(1'b0), .out(adder_13_out), .cin(adder_14_cout), .cout(adder_13_cout));
  Multiplexer multiplexer_13 (.in0(a3), .in1(adder_13_out), .out(c3), .sel(xor_1_out));
  not not_14 (not_14_out, a2);
  Adder #(.width(1)) adder_14 (.a(not_14_out), .b(1'b0), .out(adder_14_out), .cin(adder_15_cout), .cout(adder_14_cout));
  Multiplexer multiplexer_14 (.in0(a2), .in1(adder_14_out), .out(c2), .sel(xor_1_out));
  not not_15 (not_15_out, a1);
  Adder #(.width(1)) adder_15 (.a(not_15_out), .b(1'b0), .out(adder_15_out), .cin(adder_16_cout), .cout(adder_15_cout));
  Multiplexer multiplexer_15 (.in0(a1), .in1(adder_15_out), .out(c1), .sel(xor_1_out));
  not not_16 (not_16_out, a0);
  Adder #(.width(1)) adder_16 (.a(not_16_out), .b(1'b0), .out(adder_16_out), .cin(1'b1), .cout(adder_16_cout));
  Multiplexer multiplexer_16 (.in0(a0), .in1(adder_16_out), .out(c0), .sel(xor_1_out));
endmodule
